// Logisim project main.circ as structural Verilog: 4 circuits, main circuit main
module main (
  output [39:0] out_1,
  output [7:0] out_2,
  output [3:0] out_3,
  output [3:0] out_4,
  output [15:0] out_5,
  output [15:0] out_6,
  output [8:0] out_7
);

  wire ALLOW_WRITE, and_2_out, and_3_out, and_5_out, and_6_out, and_8_out, and_9_out, and_10_out, and_12_out,
       and_13_out, ARG1_POINTER, ARG1_TYPE, ARG2_POINTER, ARG2_TYPE, BEQ, BGT, BLT, BNE, CLK, clock_1_out,
       comparator_1_eq, comparator_2_eq, comparator_2_gt, comparator_2_lt, comparator_3_eq, comparator_4_eq,
       d_ff_1_q, demultiplexer_1_out0, demultiplexer_1_out1, demultiplexer_1_out2, demultiplexer_1_out3,
       demultiplexer_1_out4, demultiplexer_2_out0, demultiplexer_2_out1, demultiplexer_2_out2,
       demultiplexer_2_out3, demultiplexer_2_out4, demultiplexer_2_out5, demultiplexer_2_out6,
       demultiplexer_2_out7, demultiplexer_3_out0, demultiplexer_3_out1, demultiplexer_4_out2,
       demultiplexer_5_out1, FLAG_VALUE, HALT, MEM_WE, not_1_out, not_2_out, not_3_out, not_4_out, or_2_out,
       or_3_out, or_4_out, or_5_out, RESET, STOP_VIDEO, VIDEO_REFRESH, X_POS_carry;
  wire [2:0] bit_extender_1_out, bit_extender_2_out, undriven;
  wire [5:0] rgb_video_1_p5, X_POS_q;
  wire [8:0] counter_1_q;
  wire [15:0] adder_1_out, adder_2_out, ADDR_MEM, ARG1_REG_VALUE, ARG2_REG_VALUE, bit_extender_3_out,
       bit_extender_4_out, CST_R0, CST_R1, divider_1_out, get_addr_target_1_out_4, get_addr_target_2_out_4,
       multiplexer_1_out, multiplexer_5_out, multiplexer_6_out, multiplexer_7_out, multiplexer_9_out,
       multiplier_1_out, multiplier_2_out, R2_q, R3_q, R4_q, R5_q, R6_q, R7_q, RES_OPERATOR, SAVE_VALUE,
       subtractor_1_out, VALUE_MEM_Q, VIDEO_ADDR;

  Clock clock_1 (.out(clock_1_out));
  Button button_1 (.out(RESET));
  and and_1 (CLK, clock_1_out, ~HALT);  // AND_Gate
  not not_1 (not_1_out, CLK);
  Adder #(.width(16)) adder_1 (.a(ARG2_REG_VALUE), .b(ARG1_REG_VALUE), .out(adder_1_out));  // open: cin, cout
  Subtractor #(.width(16)) subtractor_1 (
    .a(ARG2_REG_VALUE), .b(ARG1_REG_VALUE), .out(subtractor_1_out));  // open: bin, bout
  Multiplier #(.width(16)) multiplier_1 (
    .a(ARG2_REG_VALUE), .b(ARG1_REG_VALUE), .out(multiplier_1_out));  // open: cin, cout
  Divider #(.width(16)) divider_1 (.a(ARG2_REG_VALUE), .b(ARG1_REG_VALUE), .out(divider_1_out));  // open: upper, rem
  Multiplexer #(.width(16)) multiplexer_1 (
    .in0(ARG2_REG_VALUE), .in1({16{1'b0}}), .out(multiplexer_1_out), .sel(out_1[32]));
  is_memaddr is_memaddr_1 (.INT_ARG(out_1[31:16]), .out_2(ARG1_TYPE));
  is_memaddr is_memaddr_2 (.INT_ARG(out_1[15:0]), .out_2(ARG2_TYPE));
  Comparator #(.width(4)) comparator_1 (.a(out_1[39:36]), .b(4'b0010), .eq(comparator_1_eq));  // open: gt, lt
  Comparator #(.mode("unsigned"), .width(16)) comparator_2 (
    .a(ARG1_REG_VALUE), .b(multiplexer_1_out), .gt(comparator_2_gt), .eq(comparator_2_eq),
    .lt(comparator_2_lt));
  Comparator #(.width(4)) comparator_3 (.a(out_1[39:36]), .b(4'b0100), .eq(comparator_3_eq));  // open: gt, lt
  and and_2 (and_2_out, ~VIDEO_REFRESH, not_1_out);  // AND_Gate
  or or_1 (MEM_WE, ARG2_TYPE, ARG2_POINTER);
  Multiplexer #(.select(2), .width(16)) multiplexer_2 (
    .in0(adder_1_out), .in1(subtractor_1_out), .in2(multiplier_1_out), .in3(divider_1_out),
    .out(RES_OPERATOR), .sel(out_1[33:32]));
  Counter #(.max('h1ff), .width(9)) counter_1 (
    .clr(RESET), .load(FLAG_VALUE), .clk(and_2_out), .D(out_1[24:16]), .Q(counter_1_q));  // open: up, count, carry
  is_pointer is_pointer_1 (.REG_ARG(out_1[31:16]), .IS_MEMADDR(ARG1_TYPE), .out_3(ARG1_POINTER));
  is_pointer is_pointer_2 (.REG_ARG(out_1[15:0]), .IS_MEMADDR(ARG2_TYPE), .out_3(ARG2_POINTER));
  and and_3 (and_3_out, comparator_1_eq, CLK);
  D_Flip_Flop u_BGT (.D(comparator_2_gt), .clk(and_3_out), .Q(BGT), .reset(RESET));  // open: Qn, preset
  D_Flip_Flop u_BEQ (.D(comparator_2_eq), .clk(and_3_out), .Q(BEQ), .Qn(BNE), .reset(RESET));  // open: preset
  D_Flip_Flop u_BLT (.D(comparator_2_lt), .clk(and_3_out), .Q(BLT), .reset(RESET));  // open: Qn, preset
  D_Flip_Flop d_ff_1 (.D(comparator_3_eq), .clk(CLK), .Q(d_ff_1_q), .reset(or_2_out));  // open: Qn, preset
  or or_2 (or_2_out, RESET, STOP_VIDEO);
  and and_4 (VIDEO_REFRESH, d_ff_1_q, ~STOP_VIDEO);  // AND_Gate
  Demultiplexer #(.select(4)) demultiplexer_1 (
    .out0(demultiplexer_1_out0), .out1(demultiplexer_1_out1), .out2(demultiplexer_1_out2),
    .out3(demultiplexer_1_out3), .out4(demultiplexer_1_out4), .in(1'b1), .sel(out_1[35:32]));  // open: out5, out6, out7, out8, out9, out10, out11, out12, out13, out14, out15
  and and_5 (and_5_out, demultiplexer_1_out3, BGT);
  or or_3 (or_3_out, demultiplexer_1_out4, and_5_out, and_6_out, and_8_out, and_9_out);
  Comparator #(.width(2)) comparator_4 (.a(out_1[37:36]), .b(2'b11), .eq(comparator_4_eq));  // open: gt, lt
  ROM #(.addrWidth(9), .dataWidth(40)) PROG (.addr(counter_1_q), .data(out_1));
  and and_6 (and_6_out, demultiplexer_1_out2, BLT);
  and and_7 (FLAG_VALUE, or_3_out, comparator_4_eq);
  and and_8 (and_8_out, demultiplexer_1_out1, BNE);
  and and_9 (and_9_out, demultiplexer_1_out0, BEQ);
  Demultiplexer #(.select(3)) demultiplexer_2 (
    .out0(demultiplexer_2_out0), .out1(demultiplexer_2_out1), .out2(demultiplexer_2_out2),
    .out3(demultiplexer_2_out3), .out4(demultiplexer_2_out4), .out5(demultiplexer_2_out5),
    .out6(demultiplexer_2_out6), .out7(demultiplexer_2_out7), .in(1'b1), .sel(undriven));
  Comparator comparator_5 (.a(out_1[39:32]), .b({8{1'b1}}), .eq(HALT));  // open: gt, lt
  Demultiplexer #(.select(2)) demultiplexer_3 (
    .out0(demultiplexer_3_out0), .out1(demultiplexer_3_out1), .in(1'b1), .sel(out_1[37:36]));  // open: out2, out3
  and and_10 (and_10_out, ~ARG2_TYPE, ~ARG2_POINTER, ALLOW_WRITE);  // AND_Gate
  Register #(.trigger("high"), .width(16)) R0 (
    .D(SAVE_VALUE), .en(demultiplexer_2_out0), .clk(and_10_out), .Q(CST_R0), .clr(RESET));
  Register #(.trigger("high"), .width(16)) R1 (
    .D(SAVE_VALUE), .en(demultiplexer_2_out1), .clk(and_10_out), .Q(CST_R1), .clr(RESET));
  Register #(.trigger("high"), .width(16)) R2 (
    .D(SAVE_VALUE), .en(demultiplexer_2_out2), .clk(and_10_out), .Q(R2_q), .clr(RESET));
  Register #(.trigger("high"), .width(16)) R3 (
    .D(SAVE_VALUE), .en(demultiplexer_2_out3), .clk(and_10_out), .Q(R3_q), .clr(RESET));
  Register #(.trigger("high"), .width(16)) R4 (
    .D(SAVE_VALUE), .en(demultiplexer_2_out4), .clk(and_10_out), .Q(R4_q), .clr(RESET));
  Register #(.trigger("high"), .width(16)) R5 (
    .D(SAVE_VALUE), .en(demultiplexer_2_out5), .clk(and_10_out), .Q(R5_q), .clr(RESET));
  Register #(.trigger("high"), .width(16)) R6 (
    .D(SAVE_VALUE), .en(demultiplexer_2_out6), .clk(and_10_out), .Q(R6_q), .clr(RESET));
  Register #(.trigger("high"), .width(16)) R7 (
    .D(SAVE_VALUE), .en(demultiplexer_2_out7), .clk(and_10_out), .Q(R7_q), .clr(RESET));
  or or_4 (or_4_out, demultiplexer_3_out0, demultiplexer_3_out1);
  Multiplexer #(.select(3), .width(16)) multiplexer_3 (
    .in0(CST_R0), .in1(CST_R1), .in2(R2_q), .in3(R3_q), .in4(R4_q), .in5(R5_q), .in6(R6_q), .in7(R7_q),
    .out(ARG1_REG_VALUE), .sel(bit_extender_1_out));
  Multiplexer #(.select(3), .width(16)) multiplexer_4 (
    .in0(CST_R0), .in1(CST_R1), .in2(R2_q), .in3(R3_q), .in4(R4_q), .in5(R5_q), .in6(R6_q), .in7(R7_q),
    .out(ARG2_REG_VALUE), .sel(bit_extender_2_out));
  and and_11 (ALLOW_WRITE, or_4_out, CLK);
  Bit_Extender #(.in_width(16), .out_width(3)) bit_extender_1 (.in(out_1[31:16]), .out(bit_extender_1_out));
  or or_5 (or_5_out, ARG1_TYPE, ARG1_POINTER);
  Bit_Extender #(.in_width(16), .out_width(3)) bit_extender_2 (.in(out_1[15:0]), .out(bit_extender_2_out));
  RAM #(.addrWidth(16), .dataWidth(16)) MEMORY (
    .addr(ADDR_MEM), .we(MEM_WE), .oe(1'b1), .clk(CLK), .din(SAVE_VALUE), .dout(VALUE_MEM_Q));
  get_addr_target get_addr_target_1 (
    .INT_ARG(out_1[31:16]), .REG_VALUE(ARG1_REG_VALUE), .IS_POINTER(ARG1_POINTER),
    .out_4(get_addr_target_1_out_4));
  get_addr_target get_addr_target_2 (
    .INT_ARG(out_1[15:0]), .REG_VALUE(ARG2_REG_VALUE), .IS_POINTER(ARG2_POINTER),
    .out_4(get_addr_target_2_out_4));
  Multiplexer #(.width(16)) multiplexer_5 (
    .in0(ARG1_REG_VALUE), .in1(VALUE_MEM_Q), .out(multiplexer_5_out), .sel(or_5_out));
  Demultiplexer #(.select(2)) demultiplexer_4 (
    .out2(demultiplexer_4_out2), .in(1'b1), .sel(out_1[33:32]));  // open: out0, out1, out3
  Demultiplexer #(.select(2)) demultiplexer_5 (
    .out1(demultiplexer_5_out1), .in(1'b1), .sel(out_1[37:36]));  // open: out0, out2, out3
  Multiplexer #(.width(16)) multiplexer_6 (
    .in0(get_addr_target_1_out_4), .in1(get_addr_target_2_out_4), .out(multiplexer_6_out), .sel(MEM_WE));
  Multiplexer #(.width(16)) multiplexer_7 (
    .in0(multiplexer_5_out), .in1(out_1[31:16]), .out(multiplexer_7_out), .sel(demultiplexer_4_out2));
  Multiplexer #(.width(16)) multiplexer_8 (
    .in0(multiplexer_6_out), .in1(VIDEO_ADDR), .out(ADDR_MEM), .sel(VIDEO_REFRESH));
  // Probe on VALUE_MEM_Q
  Register #(.trigger("low"), .width(16)) register_1 (
    .D(multiplexer_9_out), .en(not_2_out), .clk(CLK), .Q(SAVE_VALUE));  // open: clr
  Multiplexer #(.width(16)) multiplexer_9 (
    .in0(multiplexer_7_out), .in1(RES_OPERATOR), .out(multiplexer_9_out), .sel(demultiplexer_5_out1));
  not not_2 (not_2_out, CLK);
  not not_3 (not_3_out, CLK);
  not not_4 (not_4_out, VIDEO_REFRESH);
  and and_12 (and_12_out, VIDEO_REFRESH, not_3_out);
  Counter #(.max('h3f), .trigger("falling"), .width(6)) X_POS (
    .Q(X_POS_q), .carry(X_POS_carry), .clk(and_12_out), .clr(not_4_out));  // open: load, D, count, up
  // RGB_Video #(.cursor("No Cursor"), .height(64), .scale(6), .width(64)) rgb_video_1: pin names not known; wires that end beside it: RESET, CLK, VIDEO_REFRESH, X_POS_q, rgb_video_1_p5, VALUE_MEM_Q[14:0]
  Counter #(.max('h3f), .trigger("falling"), .width(6)) Y_POS (
    .Q(rgb_video_1_p5), .clk(and_13_out), .clr(not_4_out));  // open: load, D, count, carry, up
  and and_13 (and_13_out, and_12_out, X_POS_carry);
  assign bit_extender_3_out = {{10{1'b0}}, rgb_video_1_p5};  // Bit_Extender bit_extender_3
  assign bit_extender_4_out = {{10{1'b0}}, X_POS_q};  // Bit_Extender bit_extender_4
  Multiplier #(.width(16)) multiplier_2 (
    .a(16'h40), .b(bit_extender_3_out), .out(multiplier_2_out));  // open: cin, cout
  Adder #(.width(16)) adder_2 (.a(multiplier_2_out), .b(bit_extender_4_out), .out(adder_2_out));  // open: cin, cout
  Adder #(.width(16)) adder_3 (.a(adder_2_out), .b(16'hf000), .out(VIDEO_ADDR));  // open: cin, cout
  Comparator #(.width(16)) comparator_6 (.a(VIDEO_ADDR), .b({16{1'b1}}), .eq(STOP_VIDEO));  // open: gt, lt

  assign out_2 = out_1[39:32];
  assign out_3 = out_1[39:36];
  assign out_4 = out_1[35:32];
  assign out_5 = out_1[31:16];
  assign out_6 = out_1[15:0];

  // Other names for the same wires on the sheet: INT_ARG2[15:0] = out_1[15:0]; INT_BITFIELD[39:0] = out_1;
  //   INT_ARG1[15:0] = out_1[31:16]; INT_OP_TYPE2[3:0] = out_1[35:32]; INT_OPCODE[7:0] = out_1[39:32];
  //   INT_OP_TYPE1[3:0] = out_1[39:36]; INT_COUNTER[8:0] = out_7

  // Notes on the sheet:
  //   contents of PROG (hex, n*v repeats v):
  //   200050000 200000001 200010002 200200003 100000013 1100020000 1000020001 1000020003 2100000000
  //   3100040000 ff00000000
endmodule

module is_memaddr (
  input  [15:0] INT_ARG,
  output out_2
);

  wire comparator_1_eq, comparator_1_gt;

  Comparator #(.width(16)) comparator_1 (
    .a(INT_ARG), .b(16'h20), .gt(comparator_1_gt), .eq(comparator_1_eq));  // open: lt
  or or_1 (out_2, comparator_1_gt, comparator_1_eq);
endmodule

module is_pointer (
  input  [15:0] REG_ARG,
  input  IS_MEMADDR,
  output out_3
);

  and and_1 (out_3, REG_ARG[4], ~IS_MEMADDR);  // AND_Gate
endmodule

module get_addr_target (
  input  [15:0] INT_ARG,
  input  [15:0] REG_VALUE,
  input  IS_POINTER,
  output [15:0] out_4
);

  Multiplexer #(.width(16)) multiplexer_1 (.in0(INT_ARG), .in1(REG_VALUE), .out(out_4), .sel(IS_POINTER));
endmodule
